# Fritzing sketch RobotKit (saved by Fritzing 0.9.1b)
breadboards: 1

parts:
  Part1 = Arduino Uno (Rev3)
  VCC1 = Battery
  S1 = SPST Switch [package=r_sw_th]
  S2 = SPST Switch [package=r_sw_th]
  J1 = Basic Servo
  IR1 = TSOP312.., 314.. [package=THT]
  M2 = DC Motor
  M3 = DC Motor
  S3 = H-Bridge with L298N
  Part3 = HC-SR04 Ultrasonic Rangemeter
  R1 = Resistor [tolerance=±5% resistance=10k package=THT]

nets:
  N1: Part1.D8, S3.IN3
  N2: Part1.D9_PWM, IR1.Data, R1.Pin_1
  N3: Part1.D10_PWM/SS, J1.pulse
  N4: Part1.D11_PWM/MOSI, S3.ENA
  N5: Part1.D12/MISO, S3.IN2
  N6: Part1.D13/SCK, S3.IN1
  N7: Part1.D0/RX, Part3.Echo
  N8: Part1.D1/TX, Part3.Trig
  N9: Part1.D4, S1.O, Part3.VCC
  N10: Part1.D6_PWM, S3.ENB
  N11: Part1.D7, S3.IN4
  N12: Part1.5V, S1.P, IR1.Vs, R1.Pin_0
  GND: Part1.GND, VCC1.-, J1.gnd, IR1.GND, S3.GND, Part3.GND
  VIN: Part1.VIN, S2.P, S3.12V
  N13: VCC1.+, S2.O
  VCC: J1.vcc, S3.5V
  N14: M2.pin_1, S3.M1-02
  N15: M2.pin_2, S3.M1-01
  N16: M3.pin_1, S3.M2-02
  N17: M3.pin_2, S3.M2-01

notes:
  Encoder 2
  - 5V
  - GND
  - DO - Pin 5 Arduino
  Encoder 1
  - 5V
  - GND
  -DO - Pin 4 Arduino

custom parts:
  H-Bridge with L298N: h-bridge
